# Fritzing sketch macro_led_lights (saved by Fritzing 0.8.7b)
breadboards: 1

parts:
  part = Basic FET N-Channel [package="TO220 [THT]"]
  part_2 = Resistor [tolerance=±5% resistance=6.8k package=THT]
  part_3 = Resistor [tolerance=±5% resistance=6.8k package=THT]
  4_8_V = 4 x AAA Battery Mount
  S1 = Square Pushbutton
  part_4 = Resistor [tolerance=±5% resistance=15 package=THT]
  LED1 = smd LED [color="Red (633nm)" package="0603 [SMD]"]
  LED2 = smd LED [color="Red (633nm)" package="0603 [SMD]"]
  LED3 = smd LED [color="Red (633nm)" package="0603 [SMD]"]
  LED4 = smd LED [color="Red (633nm)" package="0603 [SMD]"]
  part_5 = Trimmer Potentiometer [package=THT]

nets:
  N1: part.gate, part_5.wiper
  N2: part.drain, part_3.Pin_1, 4_8_V.-
  N3: part.source, LED1.cathode, LED2.cathode, LED3.cathode, LED4.cathode
  N4: part_2.Pin_0, S1.leg1, part_4.Pin_0
  N5: part_2.Pin_1, part_5.leg1
  N6: part_3.Pin_0, part_5.leg2
  N7: 4_8_V.+, S1.leg0
  N8: part_4.Pin_1, LED3.anode
